# Fritzing sketch Arduino_Pro_Mini (saved by Fritzing 0.9.3b)
breadboards: 1

parts:
  Part2 = Adafruit MAX4466 Electret Microphone Amplifier [part_number="Adafruit #1063"]
  Part1 = Arduino Pro Mini (3.3V)
  S1 = Momentary Switch [package=ksa_sealed_tac_switch]
  R1 = Rotary Potentiometer (Small) [maximum_resistance=100kΩ package=THT]
  RGB_SMD_LED1 = SMD RGB LED (WS2812) [package=5050]
  R2 = Resistor [tolerance=±5% resistance=470 package=THT]
  C1 = Electrolytic Capacitor [capacitance=1000μF package="1010 [SMD, electrolytic]"]  # not connected

nets:
  VCC: Part2.VCC, Part1.VCC
  GND: Part2.GND, Part1.GND, S1.2
  N1: Part2.OUT, Part1.A0
  N2: Part1.RAW, RGB_SMD_LED1.VCC
  N3: Part1.A2, R1.wiper
  N4: Part1.D6, R2.Pin_1
  N5: Part1.D4, S1.4
  N6: R1.leg1, RGB_SMD_LED1.DOut
  N7: RGB_SMD_LED1.DIn, R2.Pin_0

notes:
  5 Volts Input 2 Amps
  Adafruit MAX4466
  Brightness Control
  56 LEDs
  WS2812B
  Arduino Pro Mini 3.3 volts

custom parts:
  Adafruit MAX4466 Electret Microphone Amplifier: Add an ear to your project with this well-designed electret microphone amplifier. This fully assembled and tested board comes with a 20-20KHz electret microphone soldered on. For the amplification, we use the Maxim MAX4466, an op-amp specifically designed for this delicate task! The amplifier has excellent power supply noise rejection, so this amplifier sounds really good and isn't nearly as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
